# Fritzing sketch dirtlensprotov2 (saved by Fritzing 1.0.1rc)

parts:
  MCU1 = Raspberry Pi Zero 2 W
  LED2 = RGB LED (com. cathode, rgb) [package="5 mm [THT]"]
  M1 = waveshare
  LED1 = RGB LED (com. cathode, rgb) [package="5 mm [THT]"]
  S1 = SWITCH-MOMENTARY-2 [package=tactile-pth]
  LCD1 = 1_54in tft lcd
  IC1 = Rasberry Pi NIOR Camera [chip_label=IC package="DIP (Dual Inline) [THT]"]  # not connected

nets (from the schematic view):
  N1: MCU1.pin_1, MCU1.pin_17, M1.connector0
  N2: MCU1.pin_2, MCU1.pin_4
  N3: MCU1.pin_7, S1.1
  N4: MCU1.pin_8, S1.2
  N5: MCU1.pin_9, MCU1.pin_34, M1.connector11, LCD1.pin_1
  N6: MCU1.pin_13, M1.connector3
  N7: MCU1.pin_15, M1.connector4
  N8: MCU1.pin_19, LCD1.pin4
  N9: MCU1.pin_22, M1.connector7
  N10: MCU1.pin_23, LCD1.pin3
  N11: MCU1.pin_29, LCD1.pin_6, LCD1.pin_7
  N12: MCU1.pin_31, LCD1.pin_5
  N13: LED2.red_anode, M1.connector16
  N14: LED2.common_cathode, M1.connector1, M1.connector2, LED1.common_cathode
  N15: LED2.green_anode, M1.connector15
  N16: LED2.blue_anode, M1.connector14
  N17: M1.connector10, LCD1.pin2
  N18: M1.connector17, LED1.blue_anode
  N19: M1.connector18, LED1.green_anode
  N20: M1.connector19, LED1.red_anode

custom parts:
  Raspberry Pi Zero 2 W: The Raspberry Pi Zero is half the size of a Model A+, with twice the utility. A tiny Raspberry Pi that’s affordable enough for any project! · 1Ghz, Single-core CPU · 512MB RAM · Mini HDMI and USB On-The-Go ports · Micro USB power · HAT-compatible 40-pin header. Jan 2018: In this version schematic has been changed so the pins match the GPIO connector. I.e. the left hand pins are all the pins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
  1_54in tft lcd: This is the DONGKER 1.54'' LCD Display Module, SPI 240x240 1.54'' LCD Display Module ST7789 Driver 240x240 3.3V IPS LCD Display Screen Module. The 1.54" display has 240x240 color pixels.
  Rasberry Pi NIOR Camera: Camera
